# Fritzing sketch AR19_dm_module (saved by Fritzing 0.9.3b)
breadboards: 1

parts:
  부품1 = Arduino Uno (Rev3)
  8x8_LED_Modul_mit_MAX1 = 8x8 LED Modul mit MAX7219 [package=THT]

nets:
  N1: 부품1.D2, 8x8_LED_Modul_mit_MAX1.CS_Eingang
  N2: 부품1.D3_PWM, 8x8_LED_Modul_mit_MAX1.CLK_Eingang
  N3: 부품1.D4, 8x8_LED_Modul_mit_MAX1.DIN_Eingang
  N4: 부품1.5V, 8x8_LED_Modul_mit_MAX1.VCC_Eingang
  N5: 부품1.GND, 8x8_LED_Modul_mit_MAX1.GND_Eingang
